# Fritzing sketch ESP32-Devkit-v1-30pin (saved by Fritzing 0.9.9b)

parts:
  U1 = ESP32 DEVKIT V1 DOIT [part_number=ESP32S-HiLetgo]
  Part1 = GP-20U7
  CUI-enc1 = AMT22
  LSM6DSOX1 = Adafruit_LSM6DSOX

nets:
  N1: U1.3.3, Part1.VCC
  N2: U1.GPIO14, CUI-enc1.SCLK
  N3: U1.GPIO12, CUI-enc1.MISO
  GND: U1.GND, Part1.GND, CUI-enc1.GND, LSM6DSOX1.GND
  N4: U1.GPIO13, CUI-enc1.MOSI
  VIN: U1.VIN, CUI-enc1.+5V
  N5: U1.GPIO15, CUI-enc1.CS
  N6: U1.GPIO4, LSM6DSOX1.VCC
  N7: U1.GPIO16, Part1.TX
  N8: U1.GPIO21, LSM6DSOX1.SDA
  N9: U1.GPIO22, LSM6DSOX1.SCL

custom parts:
  ESP32 DEVKIT V1 DOIT: 30GPIO Version
  AMT22: CUI AMT Absolute Encoders Capacitive Modular Encoders 28 mm, 12 or 14 Bit, Single-turn or multi-turn
